# Fritzing sketch bain (saved by Fritzing 0.9.3b)
circuit board: 10cm x 6cm
breadboards: 1

parts:
  Part1 = Adafruit BME280
  Part2 = Adafruit Feather HUZZAH ESP8266 [part_number="Adafruit #2821"]

nets (from the breadboard view):
  VIN: Part1.VIN, Part2.3.3V
  GND: Part1.GND, Part2.GND
  N1: Part1.SCK/SCL, Part2.GPIO4/SDA
  N2: Part1.SDI/SDA, Part2.GPIO5/SCL
  N3: Part2.RESET, Part2.GPIO16

notes:
  Deep Sleep

custom parts:
  Adafruit BME280: Bosch has stepped up their game with their new BME280 sensor, an environmental sensor with temperature, barometric pressure and humidity! This sensor is great for all sorts of weather/environmental sensing and can even be used in both I2C and SPI! This precision sensor from Bosch is the best low-cost sensing solution for measuring humidity with ±3% accuracy, barometric pressure with ±1 hPa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
  Adafruit Feather HUZZAH ESP8266: his is the Adafruit Feather HUZZAH ESP8266 - our take on an 'all-in-one' ESP8266 WiFi development board with built in USB and battery charging. Its an ESP8266 WiFi module with all the extras you need, ready to rock! We have other boards in the Feather family, check'em out here. At the Feather HUZZAH's heart is an ESP8266 WiFi microcontroller clocked at 80 MHz and at 3.3V logic. This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
