# Fritzing sketch bain_battery_monitor (saved by Fritzing 0.9.3b)
breadboards: 1

parts:
  Part4 = Adafruit Feather HUZZAH ESP8266 [part_number="Adafruit #2821"]
  R1 = Resistor [tolerance=±5% resistance=10k package=THT]
  R5 = Resistor [tolerance=±5% resistance=47k package=THT]
  R6 = Resistor [tolerance=±5% resistance=1M package=THT]
  C1 = Electrolytic Capacitor [capacitance=1µF package="0807 [SMD, electrolytic]"]

nets:
  N1: Part4.ADC, R6.Pin_0, C1.+
  N2: Part4.GND, R1.Pin_1, C1.-
  N3: Part4.VBUS, R5.Pin_0
  N4: R1.Pin_0, R5.Pin_1, R6.Pin_1

notes:
  47 kΩ
  10 kΩ
  1 µF
  1 MΩ

custom parts:
  Adafruit Feather HUZZAH ESP8266: his is the Adafruit Feather HUZZAH ESP8266 - our take on an 'all-in-one' ESP8266 WiFi development board with built in USB and battery charging. Its an ESP8266 WiFi module with all the extras you need, ready to rock! We have other boards in the Feather family, check'em out here. At the Feather HUZZAH's heart is an ESP8266 WiFi microcontroller clocked at 80 MHz and at 3.3V logic. This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
