# Fritzing sketch bain_final_assembly (saved by Fritzing 0.9.3b)

parts:
  proto1 = Adafruit Feather Wing Proto
  Composant1 = Adafruit BME280
  R8 = Resistor [tolerance=±5% resistance=1M package=THT]  # not connected
  R7 = Resistor [tolerance=±5% resistance=10k package=THT]  # not connected
  C2 = Electrolytic Capacitor [capacitance=1µF package="100 mil [THT, electrolytic]"]  # not connected
  R9 = Resistor [tolerance=±5% resistance=47k package=THT]  # not connected

nets:
  N1: proto1.connector19, proto1.connector121
  N2: proto1.connector36, Composant1.VIN
  N3: proto1.connector43, Composant1.GND
  N4: proto1.connector44, proto1.connector71
  N5: proto1.connector45, proto1.connector159
  N6: proto1.connector55, proto1.connector79
  N7: proto1.connector67, proto1.connector156
  N8: proto1.connector139, Composant1.SDI/SDA
  N9: proto1.connector148, Composant1.SCK/SCL

custom parts:
  Adafruit BME280: Bosch has stepped up their game with their new BME280 sensor, an environmental sensor with temperature, barometric pressure and humidity! This sensor is great for all sorts of weather/environmental sensing and can even be used in both I2C and SPI! This precision sensor from Bosch is the best low-cost sensing solution for measuring humidity with ±3% accuracy, barometric pressure with ±1 hPa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
